// Logisim project SOP_NAND.circ as structural Verilog: 1 circuit, main circuit main
module main (
  input  a,
  input  b,
  input  c,
  input  d,
  output x
);

  wire nand_1_out, nand_2_out, nand_3_out, nand_4_out, nand_5_out, nand_6_out, nand_7_out, nand_8_out,
       nand_9_out, nand_10_out, nand_11_out, nand_12_out, nand_13_out, nand_14_out, nand_15_out, nand_16_out,
       nand_17_out, nand_18_out, nand_19_out, nand_20_out, nand_21_out, nand_22_out, nand_23_out,
       nand_24_out, nand_25_out, nand_26_out, nand_27_out, nand_28_out, nand_29_out, nand_30_out,
       nand_31_out, nand_32_out;

  nand nand_1 (nand_1_out, a, a);
  nand nand_2 (nand_2_out, b, b);
  nand nand_3 (nand_3_out, c, c);
  nand nand_4 (nand_4_out, a, a);
  nand nand_5 (nand_5_out, b, b);
  nand nand_6 (nand_6_out, a, a);
  nand nand_7 (nand_7_out, c, c);
  nand nand_8 (nand_8_out, a, a);
  nand nand_9 (nand_9_out, d, d);
  nand nand_10 (nand_10_out, b, b);
  nand nand_11 (nand_11_out, c, c);
  nand nand_12 (nand_12_out, a, a);
  nand nand_13 (nand_13_out, c, c);
  nand nand_14 (nand_14_out, d, d);
  nand nand_15 (nand_15_out, a, a);
  nand nand_16 (nand_16_out, b, b);
  nand nand_17 (nand_17_out, c, c);
  nand nand_18 (nand_18_out, a, a);
  nand nand_19 (nand_19_out, b, b);
  nand nand_20 (nand_20_out, c, c);
  nand nand_21 (nand_21_out, d, d);
  nand nand_22 (nand_22_out, a, b, c, d);
  nand nand_23 (nand_23_out, nand_1_out, b, c, d);
  nand nand_24 (nand_24_out, a, nand_2_out, c, d);
  nand nand_25 (nand_25_out, a, b, nand_3_out, d);
  nand nand_26 (nand_26_out, nand_4_out, nand_5_out, c, d);
  nand nand_27 (nand_27_out, nand_6_out, b, nand_7_out, d);
  nand nand_28 (nand_28_out, nand_8_out, b, c, nand_9_out);
  nand nand_29 (nand_29_out, a, nand_10_out, nand_11_out, d);
  nand nand_30 (nand_30_out, nand_12_out, b, nand_13_out, nand_14_out);
  nand nand_31 (nand_31_out, nand_15_out, nand_16_out, nand_17_out, d);
  nand nand_32 (nand_32_out, nand_18_out, nand_19_out, nand_20_out, nand_21_out);
  nand nand_33 (x, nand_22_out, nand_23_out, nand_24_out, nand_25_out, nand_26_out, nand_27_out, nand_28_out, nand_29_out, nand_30_out, nand_31_out, nand_32_out);
endmodule
