// Logisim project Lab10_Counter.circ as structural Verilog: 1 circuit, main circuit main
module main (
  input  M,
  output out_2,
  output out_3,
  output out_4
);

  wire and_1_out, and_2_out, and_3_out, and_4_out, B_qn, C_qn, clock_1_out, not_1_out, or_1_out, or_2_out;

  Clock clock_1 (.out(clock_1_out));
  not not_1 (not_1_out, M);
  T_Flip_Flop C (.clk(clock_1_out), .T(1'b1), .Q(out_4), .Qn(C_qn));  // open: preset, reset, en
  and and_1 (and_1_out, not_1_out, out_4);
  and and_2 (and_2_out, M, C_qn);
  or or_1 (or_1_out, and_1_out, and_2_out);
  T_Flip_Flop B (.clk(clock_1_out), .T(or_1_out), .Q(out_3), .Qn(B_qn));  // open: preset, reset, en
  and and_3 (and_3_out, and_1_out, out_3);
  and and_4 (and_4_out, B_qn, and_2_out);
  or or_2 (or_2_out, and_3_out, and_4_out);
  T_Flip_Flop A (.clk(clock_1_out), .T(or_2_out), .Q(out_2));  // open: Qn, preset, reset, en

  // Other names for the same wires on the sheet: Qa = out_2; Qb = out_3; Qc = out_4
endmodule
