// Logisim project BCDtoE3.circ as structural Verilog: 5 circuits, main circuit main
module main (
  input  [3:0] in_1,
  output [3:0] out_2
);

  wire and_1_out, and_2_out, and_3_out, and_4_out, and_5_out, and_6_out, not_1_out, not_2_out, not_3_out,
       not_4_out, not_5_out;

  not not_1 (not_1_out, in_1[2]);
  not not_2 (not_2_out, in_1[2]);
  not not_3 (not_3_out, in_1[0]);
  not not_4 (not_4_out, in_1[1]);
  not not_5 (not_5_out, in_1[1]);
  not not_6 (out_2[0], in_1[0]);
  xnor xnor_1 (out_2[1], in_1[0], in_1[1]);
  and and_1 (and_1_out, in_1[0], not_1_out);
  and and_2 (and_2_out, in_1[1], not_2_out);
  and and_3 (and_3_out, not_3_out, not_4_out, in_1[2]);
  and and_4 (and_4_out, not_5_out, in_1[3]);
  and and_5 (and_5_out, in_1[0], in_1[2]);
  and and_6 (and_6_out, in_1[1], in_1[2]);
  or or_1 (out_2[2], and_1_out, and_2_out, and_3_out);
  or or_2 (out_2[3], and_4_out, and_5_out, and_6_out);
endmodule

module onlynands (
  input  B3,
  input  B2,
  input  B1,
  input  B0,
  output E3,
  output E2,
  output E1,
  output E0
);

  wire nand_1_out, nand_2_out, nand_4_out, nand_5_out, nand_6_out, nand_7_out, nand_8_out, nand_9_out,
       nand_10_out, nand_11_out;

  nand nand_1 (nand_1_out, B2, B2);
  nand nand_2 (nand_2_out, B1, B1);
  nand nand_3 (E0, B0, B0);
  nand nand_4 (nand_4_out, B3, B3);
  nand nand_5 (nand_5_out, B0, B2);
  nand nand_6 (nand_6_out, B1, B2);
  nand nand_7 (nand_7_out, B0, nand_1_out);
  nand nand_8 (nand_8_out, B1, nand_1_out);
  nand nand_9 (nand_9_out, E0, nand_2_out, B2);
  nand nand_10 (nand_10_out, B0, B1);
  nand nand_11 (nand_11_out, E0, nand_2_out);
  nand nand_12 (E3, nand_4_out, nand_5_out, nand_6_out);
  nand nand_13 (E2, nand_7_out, nand_8_out, nand_9_out);
  nand nand_14 (E1, nand_10_out, nand_11_out);
endmodule

module only2nands (
  input  B3,
  input  B2,
  input  B1,
  input  B0,
  output E3,
  output E2,
  output E1,
  output E0
);

  wire nand_1_out, nand_2_out, nand_4_out, nand_5_out, nand_6_out, nand_7_out, nand_8_out, nand_9_out,
       nand_10_out, nand_11_out, nand_12_out, nand_13_out, nand_14_out, nand_15_out;

  nand nand_1 (nand_1_out, B2, B2);
  nand nand_2 (nand_2_out, B1, B1);
  nand nand_3 (E0, B0, B0);
  nand nand_4 (nand_4_out, B3, B3);
  nand nand_5 (nand_5_out, B0, B2);
  nand nand_6 (nand_6_out, B1, B2);
  nand nand_7 (nand_7_out, B0, nand_1_out);
  nand nand_8 (nand_8_out, B1, nand_1_out);
  nand nand_9 (nand_9_out, E0, nand_2_out, B2);
  nand nand_10 (nand_10_out, nand_4_out, nand_5_out);
  nand nand_11 (nand_11_out, nand_7_out, nand_8_out);
  nand nand_12 (nand_12_out, B0, B1);
  nand nand_13 (nand_13_out, E0, nand_2_out);
  nand nand_14 (nand_14_out, nand_10_out, nand_10_out);
  nand nand_15 (nand_15_out, nand_11_out, nand_11_out);
  nand nand_16 (E1, nand_12_out, nand_13_out);
  nand nand_17 (E3, nand_14_out, nand_6_out);
  nand nand_18 (E2, nand_15_out, nand_9_out);
endmodule

module onlynors (
  input  B3,
  input  B2,
  input  B1,
  input  B0,
  output E3,
  output E2,
  output E1,
  output E0
);

  wire nor_1_out, nor_2_out, nor_4_out, nor_5_out, nor_6_out, nor_7_out, nor_8_out, nor_9_out, nor_10_out;

  nor nor_1 (nor_1_out, B2, B2);
  nor nor_2 (nor_2_out, B1, B1);
  nor nor_3 (E0, B0, B0);
  nor nor_4 (nor_4_out, B3, B2);
  nor nor_5 (nor_5_out, B0, B2, B3);
  nor nor_6 (nor_6_out, nor_1_out, E0);
  nor nor_7 (nor_7_out, nor_1_out, nor_2_out);
  nor nor_8 (nor_8_out, B2, B1, B0);
  nor nor_9 (nor_9_out, nor_2_out, B0);
  nor nor_10 (nor_10_out, E0, B1);
  nor nor_11 (E3, nor_4_out, nor_5_out);
  nor nor_12 (E2, nor_6_out, nor_7_out, nor_8_out);
  nor nor_13 (E1, nor_9_out, nor_10_out);
endmodule

module only2nors (
  input  B3,
  input  B2,
  input  B1,
  input  B0,
  output E3,
  output E2,
  output E1,
  output E0
);

  wire nor_1_out, nor_2_out, nor_4_out, nor_5_out, nor_6_out, nor_7_out, nor_8_out, nor_9_out, nor_10_out,
       nor_11_out, nor_12_out, nor_13_out, nor_14_out;

  nor nor_1 (nor_1_out, B2, B2);
  nor nor_2 (nor_2_out, B1, B1);
  nor nor_3 (E0, B0, B0);
  nor nor_4 (nor_4_out, B0, B2);
  nor nor_5 (nor_5_out, B2, B1);
  nor nor_6 (nor_6_out, nor_4_out, nor_4_out);
  nor nor_7 (nor_7_out, nor_5_out, nor_5_out);
  nor nor_8 (nor_8_out, B3, B2);
  nor nor_9 (nor_9_out, nor_6_out, B3);
  nor nor_10 (nor_10_out, nor_1_out, E0);
  nor nor_11 (nor_11_out, nor_1_out, nor_2_out);
  nor nor_12 (nor_12_out, nor_7_out, B0);
  nor nor_13 (nor_13_out, nor_2_out, B0);
  nor nor_14 (nor_14_out, E0, B1);
  nor nor_15 (E3, nor_8_out, nor_9_out);
  nor nor_16 (E2, nor_10_out, nor_11_out, nor_12_out);
  nor nor_17 (E1, nor_13_out, nor_14_out);
endmodule
