// Logisim project adder_substractor.circ as structural Verilog: 8 circuits, main circuit main
module main (
  input  in_1,
  input  in_2,
  output S,
  output C
);

  xor xor_1 (S, in_1, in_2);
  and and_1 (C, in_1, in_2);
endmodule

module fulladder (
  input  in_1,
  input  in_2,
  input  in_3,
  output out_4,
  output C
);

  wire and_1_out, and_2_out, xor_1_out;

  xor xor_1 (xor_1_out, in_1, in_3);
  and and_1 (and_1_out, in_1, in_3);
  xor xor_2 (out_4, xor_1_out, in_2);
  and and_2 (and_2_out, in_2, and_1_out);
  or or_1 (C, and_2_out, and_1_out);
endmodule

module _4bitadder (
  input  A3,
  input  B3,
  input  A2,
  input  B2,
  input  A1,
  input  B1,
  input  A0,
  input  B0,
  input  in_9,
  output C3,
  output S3,
  output S2,
  output S1,
  output S0
);

  wire fulladder_2_c, fulladder_3_c, fulladder_4_c;

  fulladder fulladder_1 (.in_1(B3), .in_2(fulladder_2_c), .in_3(A3), .out_4(S3), .C(C3));
  fulladder fulladder_2 (.in_1(B2), .in_2(fulladder_3_c), .in_3(A2), .out_4(S2), .C(fulladder_2_c));
  fulladder fulladder_3 (.in_1(B1), .in_2(fulladder_4_c), .in_3(A1), .out_4(S1), .C(fulladder_3_c));
  fulladder fulladder_4 (.in_1(B0), .in_2(in_9), .in_3(A0), .out_4(S0), .C(fulladder_4_c));
endmodule

module alternate_fulladder (
  input  in_1,
  input  in_2,
  input  in_3,
  output out_4,
  output out_5
);

  wire main_1_c, main_1_s, main_2_c;

  main main_1 (.in_1(in_1), .in_2(in_2), .S(main_1_s), .C(main_1_c));
  main main_2 (.in_1(main_1_s), .in_2(in_3), .S(out_4), .C(main_2_c));
  or or_1 (out_5, main_2_c, main_1_c);
endmodule

module add_substract (
  input  B2,
  input  B1,
  input  A2,
  input  A1,
  input  A0,
  input  A3,
  input  B3,
  input  B0,
  input  in_9,
  output out_10,
  output out_11,
  output out_12,
  output out_13,
  output out_14
);

  wire xor_1_out, xor_2_out, xor_3_out, xor_4_out;

  xor xor_1 (xor_1_out, B3, in_9);
  xor xor_2 (xor_2_out, B1, in_9);
  xor xor_3 (xor_3_out, B2, in_9);
  _4bitadder _4_bit_adder (
    .A3(A3), .B3(xor_1_out), .A2(A2), .B2(xor_3_out), .A1(A1), .B1(xor_2_out), .A0(A0), .B0(xor_4_out),
    .C3(out_10), .S3(out_11), .S2(out_12), .S1(out_13), .S0(out_14), .in_9(in_9));
  xor xor_4 (xor_4_out, B0, in_9);
endmodule

module alternate4adder (
  input  A3,
  input  B3,
  input  A2,
  input  B2,
  input  A1,
  input  B1,
  input  A0,
  input  B0,
  input  in_9,
  output C3,
  output S3,
  output S2,
  output S1,
  output S0
);

  wire alternate_fulladder_2_out_5, alternate_fulladder_3_out_5, alternate_fulladder_4_out_5;

  alternate_fulladder alternate_fulladder_1 (
    .in_1(B3), .in_2(A3), .in_3(alternate_fulladder_2_out_5), .out_4(S3), .out_5(C3));
  alternate_fulladder alternate_fulladder_2 (
    .in_1(B2), .in_2(A2), .in_3(alternate_fulladder_3_out_5), .out_4(S2), .out_5(alternate_fulladder_2_out_5));
  alternate_fulladder alternate_fulladder_3 (
    .in_1(B1), .in_2(A1), .in_3(alternate_fulladder_4_out_5), .out_4(S1), .out_5(alternate_fulladder_3_out_5));
  alternate_fulladder alternate_fulladder_4 (
    .in_1(in_9), .in_2(B0), .in_3(A0), .out_4(S0), .out_5(alternate_fulladder_4_out_5));
endmodule

module alternate_add_substract (
  input  A3,
  input  A2,
  input  A1,
  input  A0,
  input  B3,
  input  B2,
  input  B1,
  input  B0,
  input  in_9,
  output out_10,
  output out_11,
  output out_12,
  output out_13,
  output out_14
);

  wire xor_1_out, xor_2_out, xor_3_out, xor_4_out;

  xor xor_1 (xor_1_out, B3, in_9);
  xor xor_2 (xor_2_out, B2, in_9);
  alternate4adder alternate4adder_1 (
    .A3(A3), .B3(xor_1_out), .A2(A2), .B2(xor_2_out), .A1(A1), .B1(xor_4_out), .A0(A0), .B0(xor_3_out),
    .C3(out_10), .S3(out_11), .S2(out_12), .S1(out_13), .S0(out_14), .in_9(in_9));
  xor xor_3 (xor_3_out, B0, in_9);
  xor xor_4 (xor_4_out, B1, in_9);
endmodule

module half_subtractor (
  input  A,
  input  B,
  output D,
  output B0
);

  wire not_1_out;

  not not_1 (not_1_out, A);
  xor xor_1 (D, A, B);
  and and_1 (B0, not_1_out, B);
endmodule
