// Logisim project decoder.circ as structural Verilog: 2 circuits, main circuit decoder
module decoder (
  input  W3,
  input  W2,
  input  W1,
  input  W0,
  input  EN,
  output A,
  output B,
  output C,
  output D,
  output E,
  output F,
  output G
);

  wire and_1_out, and_2_out, and_3_out, and_4_out, and_5_out, and_6_out, and_7_out, and_8_out, and_9_out,
       and_10_out, and_11_out, and_12_out, and_13_out, and_14_out, and_15_out, and_16_out, and_17_out,
       not_1_out, not_2_out, not_3_out, or_1_out, or_2_out, or_3_out, or_4_out, or_5_out, or_6_out, or_7_out,
       or_8_out, or_9_out, or_10_out, or_11_out, or_12_out, or_13_out, or_14_out, or_15_out, or_16_out,
       or_17_out, or_18_out;

  not not_1 (not_1_out, W2);
  not not_2 (not_2_out, W1);
  not not_3 (not_3_out, W0);
  and and_1 (and_1_out, W2, W0);
  and and_2 (and_2_out, not_1_out, not_3_out);
  and and_3 (and_3_out, not_2_out, not_3_out);
  and and_4 (and_4_out, W1, W0);
  or or_1 (or_1_out, not_2_out, W0);
  and and_5 (and_5_out, W2, not_2_out);
  and and_6 (and_6_out, and_5_out, W0);
  and and_7 (and_7_out, W1, not_3_out);
  and and_8 (and_8_out, not_1_out, W1);
  and and_9 (and_9_out, not_1_out, not_3_out);
  and and_10 (and_10_out, not_1_out, not_3_out);
  and and_11 (and_11_out, W1, not_3_out);
  and and_12 (and_12_out, W2, not_3_out);
  and and_13 (and_13_out, not_2_out, not_3_out);
  and and_14 (and_14_out, W2, not_2_out);
  and and_15 (and_15_out, W2, not_2_out);
  and and_16 (and_16_out, not_1_out, W1);
  and and_17 (and_17_out, W2, not_3_out);
  or or_2 (or_2_out, and_1_out, and_2_out);
  or or_3 (or_3_out, and_3_out, and_4_out);
  or or_4 (or_4_out, or_1_out, W2);
  or or_5 (or_5_out, and_6_out, and_7_out);
  or or_6 (or_6_out, and_10_out, and_11_out);
  or or_7 (or_7_out, and_12_out, and_13_out);
  or or_8 (or_8_out, and_15_out, and_16_out);
  or or_9 (or_9_out, or_2_out, W1);
  or or_10 (or_10_out, or_3_out, not_1_out);
  or or_11 (or_11_out, or_5_out, and_8_out);
  or or_12 (or_12_out, or_7_out, and_14_out);
  or or_13 (or_13_out, or_8_out, and_17_out);
  or or_14 (or_14_out, or_9_out, W3);
  or or_15 (or_15_out, or_11_out, and_9_out);
  or or_16 (or_16_out, or_12_out, W3);
  or or_17 (or_17_out, or_13_out, W3);
  or or_18 (or_18_out, or_15_out, W3);
  and and_18 (A, or_14_out, EN);
  and and_19 (B, or_10_out, EN);
  and and_20 (C, or_4_out, EN);
  and and_21 (D, or_18_out, EN);
  and and_22 (E, or_6_out, EN);
  and and_23 (F, or_16_out, EN);
  and and_24 (G, or_17_out, EN);
endmodule

module main (
  input  in_1,
  input  in_2,
  input  in_3,
  input  in_4,
  input  EN
);

  wire decoder_1_a, decoder_1_b, decoder_1_c, decoder_1_d, decoder_1_e, decoder_1_f, decoder_1_g;

  _7_Segment_Display u_7_segment_display_1 (
    .g(decoder_1_g), .f(decoder_1_f), .a(decoder_1_a), .b(decoder_1_b), .e(decoder_1_e), .d(decoder_1_d),
    .c(decoder_1_c));  // open: dp
  decoder decoder_1 (
    .W3(in_1), .W2(in_2), .W1(in_3), .W0(in_4), .EN(EN), .A(decoder_1_a), .B(decoder_1_b), .C(decoder_1_c),
    .D(decoder_1_d), .E(decoder_1_e), .F(decoder_1_f), .G(decoder_1_g));
endmodule
