// Logisim project 4 Bit Comparator.circ as structural Verilog: 1 circuit, main circuit main
module main (
  input  A3,
  input  A2,
  input  A1,
  input  A0,
  input  B3,
  input  B2,
  input  B1,
  input  B0,
  output Z,
  output X,
  output Y
);

  wire A0_prime, A1_prime, A2_prime, A3_prime, B0_prime, B1_prime, B2_prime, B3_prime, multiplexer_11_out,
       multiplexer_15_out, multiplexer_16_out, multiplexer_17_out, multiplexer_18_out, multiplexer_20_out,
       multiplexer_21_out, multiplexer_22_out, multiplexer_23_out, multiplexer_24_out, multiplexer_25_out,
       multiplexer_26_out, multiplexer_27_out, multiplexer_28_out, multiplexer_29_out, multiplexer_31_out,
       multiplexer_32_out, multiplexer_33_out, multiplexer_34_out, X0, X1, X2, X3, X3X2, X3X2X1;

  Multiplexer #(.enable("false")) multiplexer_1 (.in0(1'b1), .in1(1'b0), .out(A3_prime), .sel(A3));
  Multiplexer #(.enable("false")) multiplexer_2 (.in0(1'b1), .in1(1'b0), .out(A2_prime), .sel(A2));
  Multiplexer #(.enable("false")) multiplexer_3 (.in0(1'b1), .in1(1'b0), .out(A1_prime), .sel(A1));
  Multiplexer #(.enable("false")) multiplexer_4 (.in0(1'b1), .in1(1'b0), .out(A0_prime), .sel(A0));
  Multiplexer #(.enable("false")) multiplexer_5 (.in0(1'b1), .in1(1'b0), .out(B3_prime), .sel(B3));
  Multiplexer #(.enable("false")) multiplexer_6 (.in0(1'b1), .in1(1'b0), .out(B2_prime), .sel(B2));
  Multiplexer #(.enable("false")) multiplexer_7 (.in0(1'b1), .in1(1'b0), .out(B1_prime), .sel(B1));
  Multiplexer #(.enable("false")) multiplexer_8 (.in0(1'b1), .in1(1'b0), .out(B0_prime), .sel(B0));
  Multiplexer #(.enable("false")) multiplexer_9 (.in0(B3_prime), .in1(B3), .out(X3), .sel(A3));
  Multiplexer #(.enable("false")) multiplexer_10 (.in0(1'b0), .in1(X3), .out(X3X2), .sel(X2));
  Multiplexer #(.enable("false")) multiplexer_11 (.in0(1'b0), .in1(X1), .out(multiplexer_11_out), .sel(X0));
  Multiplexer #(.enable("false")) multiplexer_12 (.in0(1'b0), .in1(X3X2), .sel(X1));  // open: out
  Multiplexer #(.enable("false")) multiplexer_13 (.in0(B2_prime), .in1(B2), .out(X2), .sel(A2));
  Multiplexer #(.enable("false")) multiplexer_14 (.in0(1'b0), .in1(X3X2), .out(Z), .sel(multiplexer_11_out));
  Multiplexer #(.enable("false")) multiplexer_15 (.in0(1'b0), .in1(A3), .out(multiplexer_15_out), .sel(B3_prime));
  Multiplexer #(.enable("false")) multiplexer_16 (.in0(1'b0), .in1(A2), .out(multiplexer_16_out), .sel(B2_prime));
  Multiplexer #(.enable("false")) multiplexer_17 (.in0(1'b0), .in1(A1), .out(multiplexer_17_out), .sel(B1_prime));
  Multiplexer #(.enable("false")) multiplexer_18 (.in0(1'b0), .in1(A0), .out(multiplexer_18_out), .sel(B0_prime));
  Multiplexer #(.enable("false")) multiplexer_19 (.in0(1'b0), .in1(X1), .out(X3X2X1), .sel(X3X2));
  Multiplexer #(.enable("false")) multiplexer_20 (.in0(1'b0), .in1(B3), .out(multiplexer_20_out), .sel(A3_prime));
  Multiplexer #(.enable("false")) multiplexer_21 (.in0(1'b0), .in1(B2), .out(multiplexer_21_out), .sel(A2_prime));
  Multiplexer #(.enable("false")) multiplexer_22 (.in0(1'b0), .in1(B1), .out(multiplexer_22_out), .sel(A1_prime));
  Multiplexer #(.enable("false")) multiplexer_23 (.in0(1'b0), .in1(B0), .out(multiplexer_23_out), .sel(A0_prime));
  Multiplexer #(.enable("false")) multiplexer_24 (
    .in0(1'b0), .in1(multiplexer_16_out), .out(multiplexer_24_out), .sel(X3));
  Multiplexer #(.enable("false")) multiplexer_25 (
    .in0(1'b0), .in1(multiplexer_18_out), .out(multiplexer_25_out), .sel(X3X2X1));
  Multiplexer #(.enable("false")) multiplexer_26 (
    .in0(1'b0), .in1(multiplexer_21_out), .out(multiplexer_26_out), .sel(X3));
  Multiplexer #(.enable("false")) multiplexer_27 (
    .in0(1'b0), .in1(multiplexer_22_out), .out(multiplexer_27_out), .sel(X3X2));
  Multiplexer #(.enable("false")) multiplexer_28 (
    .in0(1'b0), .in1(multiplexer_23_out), .out(multiplexer_28_out), .sel(X3X2X1));
  Multiplexer #(.enable("false")) multiplexer_29 (
    .in0(1'b0), .in1(multiplexer_17_out), .out(multiplexer_29_out), .sel(X3X2));
  Multiplexer #(.enable("false")) multiplexer_30 (.in0(B1_prime), .in1(B1), .out(X1), .sel(A1));
  Multiplexer #(.enable("false")) multiplexer_31 (
    .in0(multiplexer_15_out), .in1(1'b1), .out(multiplexer_31_out), .sel(multiplexer_24_out));
  Multiplexer #(.enable("false")) multiplexer_32 (
    .in0(multiplexer_29_out), .in1(1'b1), .out(multiplexer_32_out), .sel(multiplexer_25_out));
  Multiplexer #(.enable("false")) multiplexer_33 (
    .in0(multiplexer_20_out), .in1(1'b1), .out(multiplexer_33_out), .sel(multiplexer_26_out));
  Multiplexer #(.enable("false")) multiplexer_34 (
    .in0(multiplexer_27_out), .in1(1'b1), .out(multiplexer_34_out), .sel(multiplexer_28_out));
  Multiplexer #(.enable("false")) multiplexer_35 (.in0(B0_prime), .in1(B0), .out(X0), .sel(A0));
  Multiplexer #(.enable("false")) multiplexer_36 ();  // open: in0, in1, out, sel
  Multiplexer #(.enable("false")) multiplexer_37 (
    .in0(multiplexer_31_out), .in1(1'b1), .out(X), .sel(multiplexer_32_out));
  Multiplexer #(.enable("false")) multiplexer_38 (
    .in0(multiplexer_33_out), .in1(1'b1), .out(Y), .sel(multiplexer_34_out));
endmodule
