// Logisim project DDL6.circ as structural Verilog: 3 circuits, main circuit main
module main (
  input  in_1,
  input  in_2,
  input  in_3,
  input  in_4,
  input  in_5,
  input  in_6,
  output out_7
);

  Using_CMOS using_cmos_1 (
    .I0(in_1), .S0(in_6), .I1(in_2), .I2(in_3), .I3(in_4), .S1(in_5), ._4_1_mux_using_CMOS(out_7));  // open: S0_prime, out_8, _4_1_MUX_using_TG
endmodule

module Using_CMOS (
  input  I0,
  input  S0,
  input  I1,
  input  I2,
  input  I3,
  input  S1,
  output S0_prime,
  output out_8,
  output _4_1_mux_using_CMOS,
  output _4_1_MUX_using_TG
);

  wire transistor_5_out, transistor_6_out, transistor_7_out, transistor_10_out, transistor_11_out,
       transistor_21_out, transistor_22_out, transistor_24_out, transistor_25_out, transistor_27_out,
       transistor_28_out, transmission_1_p4, transmission_2_p4, transmission_3_p4, transmission_4_p4;

  Transistor transistor_1 (.in(1'b1), .out(S0_prime), .gate(S0));
  Transistor #(.\type ("n")) transistor_2 (.in(1'b0), .out(S0_prime), .gate(S0));
  Transistor transistor_3 (.in(1'b1), .out(out_8), .gate(S1));
  Transistor #(.\type ("n")) transistor_4 (.in(1'b0), .out(out_8), .gate(S1));
  // Transmission_Gate transmission_1: pin names not known; wires that end beside it: I0, S1, out_8, transmission_1_p4
  // Transmission_Gate transmission_2: pin names not known; wires that end beside it: I1, S1, out_8, transmission_2_p4
  // Transmission_Gate transmission_3: pin names not known; wires that end beside it: I2, out_8, S1, transmission_3_p4
  // Transmission_Gate transmission_4: pin names not known; wires that end beside it: I3, out_8, S1, transmission_4_p4
  // Transmission_Gate transmission_5: pin names not known; wires that end beside it: transmission_1_p4, S0, S0_prime, _4_1_MUX_using_TG
  // Transmission_Gate transmission_6: pin names not known; wires that end beside it: transmission_2_p4, S0_prime, S0, _4_1_MUX_using_TG
  // Transmission_Gate transmission_7: pin names not known; wires that end beside it: transmission_3_p4, S0, S0_prime, _4_1_MUX_using_TG
  // Transmission_Gate transmission_8: pin names not known; wires that end beside it: transmission_4_p4, S0_prime, S0, _4_1_MUX_using_TG
  Transistor transistor_5 (.in(1'b0), .out(transistor_5_out), .gate(I0));
  Transistor transistor_6 (.in(transistor_5_out), .out(transistor_6_out), .gate(I1));
  Transistor transistor_7 (.in(transistor_6_out), .out(transistor_7_out), .gate(I2));
  Transistor transistor_8 (.in(transistor_7_out), .out(_4_1_mux_using_CMOS), .gate(I3));
  Transistor #(.\type ("n")) transistor_9 (.in(transistor_10_out), .out(_4_1_mux_using_CMOS), .gate(I0));
  Transistor #(.\type ("n")) transistor_10 (.in(transistor_11_out), .out(transistor_10_out), .gate(out_8));
  Transistor #(.\type ("n")) transistor_11 (.in(1'b1), .out(transistor_11_out), .gate(S0_prime));
  Transistor transistor_12 (.in(1'b0), .out(transistor_5_out), .gate(out_8));
  Transistor transistor_13 (.in(transistor_5_out), .out(transistor_6_out), .gate(out_8));
  Transistor transistor_14 (.in(transistor_6_out), .out(transistor_7_out), .gate(S1));
  Transistor transistor_15 (.in(transistor_7_out), .out(_4_1_mux_using_CMOS), .gate(S1));
  Transistor transistor_16 (.in(1'b0), .out(transistor_5_out), .gate(S0_prime));
  Transistor transistor_17 (.in(transistor_5_out), .out(transistor_6_out), .gate(S0));
  Transistor transistor_18 (.in(transistor_6_out), .out(transistor_7_out), .gate(S0_prime));
  Transistor transistor_19 (.in(transistor_7_out), .out(_4_1_mux_using_CMOS), .gate(S0));
  Transistor #(.\type ("n")) transistor_20 (.in(transistor_21_out), .out(_4_1_mux_using_CMOS), .gate(I1));
  Transistor #(.\type ("n")) transistor_21 (.in(transistor_22_out), .out(transistor_21_out), .gate(out_8));
  Transistor #(.\type ("n")) transistor_22 (.in(1'b1), .out(transistor_22_out), .gate(S0));
  Transistor #(.\type ("n")) transistor_23 (.in(transistor_24_out), .out(_4_1_mux_using_CMOS), .gate(I2));
  Transistor #(.\type ("n")) transistor_24 (.in(transistor_25_out), .out(transistor_24_out), .gate(S1));
  Transistor #(.\type ("n")) transistor_25 (.in(1'b1), .out(transistor_25_out), .gate(S0_prime));
  Transistor #(.\type ("n")) transistor_26 (.in(transistor_27_out), .out(_4_1_mux_using_CMOS), .gate(I3));
  Transistor #(.\type ("n")) transistor_27 (.in(transistor_28_out), .out(transistor_27_out), .gate(S1));
  Transistor #(.\type ("n")) transistor_28 (.in(1'b1), .out(transistor_28_out), .gate(S0));

  // Other names for the same wires on the sheet: S1_prime = out_8
endmodule

module using_TG (
  output _4_1_Complemenraty
);

  wire I0, I1, I2, I3, S0, S0_prime, S1, S1_prime, transistor_1_out, transistor_2_out, transistor_3_out,
       transistor_6_out, transistor_7_out, transistor_17_out, transistor_18_out, transistor_20_out,
       transistor_21_out, transistor_23_out, transistor_24_out;

  Transistor transistor_1 (.in(1'b1), .out(transistor_1_out), .gate(I0));
  Transistor transistor_2 (.in(transistor_1_out), .out(transistor_2_out), .gate(I1));
  Transistor transistor_3 (.in(transistor_2_out), .out(transistor_3_out), .gate(I2));
  Transistor transistor_4 (.in(transistor_3_out), .out(_4_1_Complemenraty), .gate(I3));
  Transistor #(.\type ("n")) transistor_5 (.in(transistor_6_out), .out(_4_1_Complemenraty), .gate(I0));
  Transistor #(.\type ("n")) transistor_6 (.in(transistor_7_out), .out(transistor_6_out), .gate(S1_prime));
  Transistor #(.\type ("n")) transistor_7 (.in(1'b0), .out(transistor_7_out), .gate(S0_prime));
  Transistor transistor_8 (.in(1'b1), .out(transistor_1_out), .gate(S1_prime));
  Transistor transistor_9 (.in(transistor_1_out), .out(transistor_2_out), .gate(S1_prime));
  Transistor transistor_10 (.in(transistor_2_out), .out(transistor_3_out), .gate(S1));
  Transistor transistor_11 (.in(transistor_3_out), .out(_4_1_Complemenraty), .gate(S1));
  Transistor transistor_12 (.in(1'b1), .out(transistor_1_out), .gate(S0_prime));
  Transistor transistor_13 (.in(transistor_1_out), .out(transistor_2_out), .gate(S0));
  Transistor transistor_14 (.in(transistor_2_out), .out(transistor_3_out), .gate(S0_prime));
  Transistor transistor_15 (.in(transistor_3_out), .out(_4_1_Complemenraty), .gate(S0));
  Transistor #(.\type ("n")) transistor_16 (.in(transistor_17_out), .out(_4_1_Complemenraty), .gate(I1));
  Transistor #(.\type ("n")) transistor_17 (.in(transistor_18_out), .out(transistor_17_out), .gate(S1_prime));
  Transistor #(.\type ("n")) transistor_18 (.in(1'b0), .out(transistor_18_out), .gate(S0));
  Transistor #(.\type ("n")) transistor_19 (.in(transistor_20_out), .out(_4_1_Complemenraty), .gate(I2));
  Transistor #(.\type ("n")) transistor_20 (.in(transistor_21_out), .out(transistor_20_out), .gate(S1));
  Transistor #(.\type ("n")) transistor_21 (.in(1'b0), .out(transistor_21_out), .gate(S0_prime));
  Transistor #(.\type ("n")) transistor_22 (.in(transistor_23_out), .out(_4_1_Complemenraty), .gate(I3));
  Transistor #(.\type ("n")) transistor_23 (.in(transistor_24_out), .out(transistor_23_out), .gate(S1));
  Transistor #(.\type ("n")) transistor_24 (.in(1'b0), .out(transistor_24_out), .gate(S0));
endmodule
