// Logisim project lab6.circ as structural Verilog: 2 circuits, main circuit main
module main (
  input  S0,
  input  S1,
  input  I0,
  input  I1,
  input  I2,
  input  I3,
  output Z
);

  wire not_1_out, not_2_out, transistor_1_out, transistor_5_out;

  not not_1 (not_1_out, S0);
  Transistor #(.\type ("n")) transistor_1 (.in(I0), .out(transistor_1_out), .gate(not_1_out));
  Transistor #(.gate("br")) transistor_2 (.in(I0), .out(transistor_1_out), .gate(S0));
  Transistor #(.\type ("n")) transistor_3 (.in(I1), .out(transistor_1_out), .gate(S0));
  Transistor #(.gate("br")) transistor_4 (.in(I1), .out(transistor_1_out), .gate(not_1_out));
  Transistor #(.\type ("n")) transistor_5 (.in(I2), .out(transistor_5_out), .gate(not_1_out));
  Transistor #(.gate("br")) transistor_6 (.in(I2), .out(transistor_5_out), .gate(S0));
  Transistor #(.\type ("n")) transistor_7 (.in(I3), .out(transistor_5_out), .gate(S0));
  Transistor #(.gate("br")) transistor_8 (.in(I3), .out(transistor_5_out), .gate(not_1_out));
  not not_2 (not_2_out, S1);
  Transistor #(.\type ("n")) transistor_9 (.in(transistor_1_out), .out(Z), .gate(not_2_out));
  Transistor #(.gate("br")) transistor_10 (.in(transistor_1_out), .out(Z), .gate(S1));
  Transistor #(.\type ("n")) transistor_11 (.in(transistor_5_out), .out(Z), .gate(S1));
  Transistor #(.gate("br")) transistor_12 (.in(transistor_5_out), .out(Z), .gate(not_2_out));
endmodule

// S1'
module cmos2 (
  input  in_1,
  input  in_2,
  input  in_3,
  input  in_4,
  input  in_5,
  input  in_6,
  output Z
);

  wire S0_prime, S1_prime, transistor_2_out, transistor_4_out, transistor_5_out, transistor_6_out,
       transistor_7_out, transistor_8_out, transistor_10_out, transistor_11_out, transistor_12_out,
       transistor_13_out, transistor_14_out, transistor_17_out, transistor_18_out, transistor_19_out,
       transistor_20_out, transistor_21_out, transistor_24_out, transistor_25_out, transistor_28_out,
       transistor_29_out, transistor_30_out;

  Transistor transistor_1 (.in(1'b1), .out(S1_prime), .gate(in_1));
  Transistor #(.\type ("n")) transistor_2 (.in(S1_prime), .out(transistor_2_out), .gate(in_1));
  Transistor transistor_3 (.in(1'b1), .out(S0_prime), .gate(in_2));
  Transistor #(.\type ("n")) transistor_4 (.in(S0_prime), .out(transistor_4_out), .gate(in_2));
  Transistor transistor_5 (.in(1'b1), .out(transistor_5_out), .gate(S1_prime));
  Transistor transistor_6 (.in(transistor_5_out), .out(transistor_6_out), .gate(S1_prime));
  Transistor transistor_7 (.in(transistor_6_out), .out(transistor_7_out), .gate(in_1));
  Transistor transistor_8 (.in(transistor_7_out), .out(transistor_8_out), .gate(in_1));
  Transistor #(.\type ("n")) transistor_9 (.in(transistor_10_out), .out(transistor_8_out), .gate(S1_prime));
  Transistor #(.\type ("n")) transistor_10 (.in(transistor_11_out), .out(transistor_10_out), .gate(S0_prime));
  Transistor #(.\type ("n")) transistor_11 (.in(1'b0), .out(transistor_11_out), .gate(in_6));
  Transistor transistor_12 (.in(1'b1), .out(transistor_12_out), .gate(S0_prime));
  Transistor transistor_13 (.in(transistor_12_out), .out(transistor_13_out), .gate(in_2));
  Transistor transistor_14 (.in(transistor_13_out), .out(transistor_14_out), .gate(S0_prime));
  Transistor transistor_15 (.in(transistor_14_out), .out(transistor_8_out), .gate(in_2));
  Transistor #(.\type ("n")) transistor_16 (.in(transistor_17_out), .out(transistor_8_out), .gate(S1_prime));
  Transistor #(.\type ("n")) transistor_17 (.in(transistor_18_out), .out(transistor_17_out), .gate(in_2));
  Transistor #(.\type ("n")) transistor_18 (.in(1'b0), .out(transistor_18_out), .gate(in_5));
  Transistor transistor_19 (.in(1'b1), .out(transistor_19_out), .gate(in_6));
  Transistor transistor_20 (.in(transistor_19_out), .out(transistor_20_out), .gate(in_5));
  Transistor transistor_21 (.in(transistor_20_out), .out(transistor_21_out), .gate(in_4));
  Transistor transistor_22 (.in(transistor_21_out), .out(transistor_8_out), .gate(in_3));
  Transistor #(.\type ("n")) transistor_23 (.in(transistor_24_out), .out(transistor_8_out), .gate(in_1));
  Transistor #(.\type ("n")) transistor_24 (.in(transistor_25_out), .out(transistor_24_out), .gate(S0_prime));
  Transistor #(.\type ("n")) transistor_25 (.in(1'b0), .out(transistor_25_out), .gate(in_4));
  Transistor transistor_26 (.in(1'b1), .out(Z), .gate(transistor_8_out));
  Transistor #(.\type ("n")) transistor_27 (.in(transistor_29_out), .out(transistor_8_out), .gate(in_1));
  Transistor #(.\type ("n")) transistor_28 (.in(Z), .out(transistor_28_out), .gate(transistor_8_out));
  Transistor #(.\type ("n")) transistor_29 (.in(transistor_30_out), .out(transistor_29_out), .gate(in_2));
  Transistor #(.\type ("n")) transistor_30 (.in(1'b0), .out(transistor_30_out), .gate(in_3));
  // also tied to GND on the sheet: {transistor_2_out, transistor_4_out, transistor_28_out}

  // Other names for the same wires on the sheet: I0 = in_6; I1 = in_5; I2 = in_4; I3 = in_3; S0 = in_2; S1 = in_1

  // Notes on the sheet:
  //   S1'
  //   S0'
endmodule
