// Logisim project DDL7.circ as structural Verilog: 2 circuits, main circuit JKwD
module JKwD (
  input  J,
  input  K,
  output Q,
  output Q_prime
);

  wire and_1_out, and_2_out, clock_1_out, not_1_out, or_1_out;

  not not_1 (not_1_out, K);
  and and_1 (and_1_out, Q_prime, J);
  and and_2 (and_2_out, not_1_out, Q);
  or or_1 (or_1_out, and_1_out, and_2_out);
  Clock clock_1 (.out(clock_1_out));
  D_Flip_Flop d_ff_1 (.clk(clock_1_out), .D(or_1_out), .Q(Q), .Qn(Q_prime));  // open: preset, en, reset
endmodule

module TwJK (
  input  I,
  input  in_2,
  output Q,
  output Q_prime
);

  wire clock_1_out;

  Clock clock_1 (.out(clock_1_out));
  J_K_Flip_Flop j_k_ff_1 (.J(I), .clk(clock_1_out), .K(I), .Q(Q), .Qn(Q_prime), .en(in_2));  // open: preset, reset
endmodule
