// Logisim project L8.circ as structural Verilog: 1 circuit, main circuit main
module main (
  input  in_1
);

  wire and_1_out, and_2_out, and_3_out, and_4_out, CLK, not_1_out, or_1_out, Qa_q, Qb_q, Qb_qn, xor_1_out,
       xor_2_out;

  not not_1 (not_1_out, in_1);
  and and_1 (and_1_out, not_1_out, Qa_q, Qb_qn);
  and and_2 (and_2_out, Qb_q, in_1);
  or or_1 (or_1_out, and_1_out, and_2_out);
  xor xor_1 (xor_1_out, or_1_out, Qa_q);
  Clock clock_1 (.out(CLK));
  T_Flip_Flop Qa (.clk(CLK), .T(xor_1_out), .Q(Qa_q));  // open: Qn, preset, reset, en
  and and_3 (and_3_out, in_1, Qa_q, Qb_q);
  LED led_1 (.in(and_3_out));
  and and_4 (and_4_out, not_1_out, Qb_qn);
  xor xor_2 (xor_2_out, and_4_out, Qb_q);
  T_Flip_Flop Qb (.clk(CLK), .T(xor_2_out), .Q(Qb_q), .Qn(Qb_qn));  // open: preset, reset, en
endmodule
