// Logisim project Lab9_UniversalShiftRegister.circ as structural Verilog: 1 circuit, main circuit main
module main (
  input  SIRS,
  input  [1:0] S1_S0,
  input  SILS,
  input  IN_1,
  input  IN2,
  input  IN3,
  input  IN4,
  output A,
  output B,
  output C,
  output D
);

  wire CLEAR_out, CLOCK_out, multiplexer_1_out, multiplexer_2_out, multiplexer_3_out, multiplexer_4_out;

  Clock CLOCK (.out(CLOCK_out));
  Button CLEAR (.out(CLEAR_out));
  D_Flip_Flop Da (.clk(CLOCK_out), .D(multiplexer_1_out), .Q(A), .reset(CLEAR_out));  // open: Qn, preset, en
  Multiplexer #(.select(2), .enable("false")) multiplexer_1 (
    .in0(A), .in1(SIRS), .in2(B), .in3(IN_1), .out(multiplexer_1_out), .sel(S1_S0));
  D_Flip_Flop Db (.clk(CLOCK_out), .D(multiplexer_2_out), .Q(B), .reset(CLEAR_out));  // open: Qn, preset, en
  Multiplexer #(.select(2), .enable("false")) multiplexer_2 (
    .in0(B), .in1(A), .in2(C), .in3(IN2), .out(multiplexer_2_out), .sel(S1_S0));
  D_Flip_Flop Dc (.clk(CLOCK_out), .D(multiplexer_3_out), .Q(C), .reset(CLEAR_out));  // open: Qn, preset, en
  Multiplexer #(.select(2), .enable("false")) multiplexer_3 (
    .in0(C), .in1(B), .in2(D), .in3(IN3), .out(multiplexer_3_out), .sel(S1_S0));
  D_Flip_Flop Dd (.clk(CLOCK_out), .D(multiplexer_4_out), .Q(D), .reset(CLEAR_out));  // open: Qn, preset, en
  Multiplexer #(.select(2), .enable("false")) multiplexer_4 (
    .in0(D), .in1(C), .in2(SILS), .in3(IN4), .out(multiplexer_4_out), .sel(S1_S0));
endmodule
